# Fritzing sketch yaaap (saved by Fritzing 0.9.2b)

parts:
  9DoL_MPU9250 = Magnetometer HMC5883L Breakout
  b3_up = Round Pushbutton
  b2_select = Round Pushbutton
  b1_down = Round Pushbutton
  ACS712 = ACS712 Low Current Sensor Board v12
  TB6612FNG = Motor Driver 1A Dual TB6612FNG
  DC-DC_12V-5V = DC-DC_CONVERTER [package=dc-dc_converter]
  tiller_motor = DC Motor
  12C_LCD = Grove OLED 128x96
  pro_mini = Arduino Pro Mini v13
  R1_backlight = Resistor [tolerance=±5% resistance=220 package=THT]
  Diode = Rectifier Diode [part_number=1N4001 package="Melf DO-213 AB [SMD]"]
  6A_fuse = Fuse with Handler [part_number=Htc-15m]
  12V_supply = LilyPad Simple Power

nets:
  VCC: 9DoL_MPU9250.VCC_+5V, ACS712.5V, TB6612FNG.VCC, DC-DC_12V-5V.SENSE, 12C_LCD.VCC, pro_mini.VCC
  GND: 9DoL_MPU9250.GND, ACS712.GND, TB6612FNG.GND, DC-DC_12V-5V.VOUT, DC-DC_12V-5V.GND2, 12C_LCD.GND, Diode.anode, 12V_supply.GND
  N1: 9DoL_MPU9250.SCL, 12C_LCD.SCL, pro_mini.A5
  N2: 9DoL_MPU9250.SDA, 12C_LCD.SDA, pro_mini.A4
  N3: b3_up.leg0, b2_select.leg0, b1_down.leg0, pro_mini.GND
  N4: b3_up.leg1, pro_mini.A3
  N5: b2_select.leg1, pro_mini.A2
  N6: b1_down.leg1, pro_mini.A1
  N7: ACS712.VO, pro_mini.D2
  N8: ACS712.IP+, tiller_motor.pin_2
  N9: ACS712.IP-, TB6612FNG.B01, TB6612FNG.A01
  N10: TB6612FNG.B02, TB6612FNG.A02, tiller_motor.pin_1
  N11: TB6612FNG.VM, DC-DC_12V-5V.SEQ, 6A_fuse.Connector2
  N12: TB6612FNG.PWMA, pro_mini.D3_PWM
  N13: TB6612FNG.AIN2, pro_mini.D4
  N14: TB6612FNG.AIN1, pro_mini.D5_PWM
  N15: TB6612FNG.STBY, pro_mini.D6_PWM
  N16: TB6612FNG.BIN1, pro_mini.D7
  N17: TB6612FNG.BIN2, pro_mini.D8
  N18: TB6612FNG.PWMB, pro_mini.D9_PWM
  N19: pro_mini.D10_PWM/SS, R1_backlight.Pin_0
  N20: Diode.cathode, 6A_fuse.Connector1, 12V_supply.+

custom parts:
  Magnetometer HMC5883L Breakout: This is a breakout board for Honeywell's HMC5883, a 3-axis digital compass. Communication with the HMC5883 is simple and all done through an I2C interface. There is no on-board regulator, so a regulated voltage of 2.16-3.6VDC should be supplied. The breakout board includes the HMC584843 sensor and all filtering capacitors as shown. The power and 2-wire interface pins are all broken out to a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
